# Fritzing sketch protype1 (saved by Fritzing 0.9.3b)
circuit board: 4cm x 5cm
breadboards: 1

parts:
  R9 = Resistor [tolerance=±5% resistance=2k package=THT]
  R7 = Resistor [tolerance=±5% resistance=820 package=THT]
  R5 = Resistor [tolerance=±5% resistance=820 package=THT]
  LED1 = LED - 5mm [color="Red (633nm)" package="5 mm [THT]"]
  LED2 = LED - 5mm [color="Red (633nm)" package="5 mm [THT]"]
  Q4 = NPN-Transistor [package="TO92 [THT]"]
  R4 = Resistor [tolerance=±5% resistance=820 package=THT]
  R2 = Resistor [tolerance=±5% resistance=820 package=THT]
  J1 = female pin header, 2 pins [form="♀ (female)"]
  J2 = female pin header, 2 pins [form="♀ (female)"]
  R11 = Resistor [tolerance=±5% resistance=4k package=THT]
  R12 = Resistor [tolerance=±5% resistance=4k package=THT]
  Q7 = NPN-Transistor [package="TO92 [THT]"]
  Q5 = NPN-Transistor [package="TO92 [THT]"]
  Q9 = NPN-Transistor [package="TO92 [THT]"]
  Q11 = PNP-Transistor [package="TO92 [THT]"]
  Q12 = PNP-Transistor [package="TO92 [THT]"]

nets:
  N1: R9.Pin_0, LED1.anode, LED2.cathode
  N2: R9.Pin_1, J1.pin1
  N3: R7.Pin_0, Q7.B
  GPIO22: R7.Pin_1
  GPIO17: R5.Pin_0
  N4: R5.Pin_1, Q5.B
  N5: LED1.cathode, LED2.anode, J2.pin2
  GND: Q4.E, Q7.E, Q5.E, Q9.E
  N6: Q4.B, R4.Pin_1
  N7: Q4.C, R12.Pin_1
  GPIO23: R4.Pin_0
  N8: R2.Pin_0, Q9.B
  GPIO18: R2.Pin_1
  N9: J1.pin2, Q7.C, Q12.E
  N10: J2.pin1, Q5.C, Q11.E
  N11: R11.Pin_0, Q12.B
  N12: R11.Pin_1, Q9.C
  N13: R12.Pin_0, Q11.B
  30V: Q11.C, Q12.C

custom parts:
  PNP-Transistor: A standard PNP signal transistor
